# Fritzing sketch sketch (saved by Fritzing 0.9.3b)
breadboards: 1

parts:
  Raspberry_Pi_Zero1 = Raspberry Pi Zero
  LED1 = LED - 5mm [color="White (6500K)" package="5 mm [THT]"]
  LED2 = LED - 5mm [color="Blue (430nm)" package="5 mm [THT]"]
  LED3 = LED - 5mm [color="Green (555nm)" package="5 mm [THT]"]
  LED4 = LED - 5mm [color="Yellow (592nm)" package="5 mm [THT]"]
  LED5 = LED - 5mm [color="Red (633nm)" package="5 mm [THT]"]
  LED6 = LED - 5mm [color="White (6500K)" package="5 mm [THT]"]

nets:
  N1: Raspberry_Pi_Zero1.GPIO10, LED6.anode
  N2: Raspberry_Pi_Zero1.GPIO9, LED2.anode
  N3: Raspberry_Pi_Zero1.GPIO11, LED3.anode
  N4: Raspberry_Pi_Zero1.GPIO7, LED1.anode
  N5: Raspberry_Pi_Zero1.GPIO8, LED5.anode
  N6: Raspberry_Pi_Zero1.GPIO25, LED4.anode
  N7: Raspberry_Pi_Zero1.GND, LED1.cathode, LED2.cathode, LED3.cathode, LED4.cathode, LED5.cathode, LED6.cathode
